// Logisim project dekoder_multiplexor.circ as structural Verilog: 3 circuits, main circuit main
module main (
  input  A,
  input  B,
  input  C,
  input  D,
  input  [1:0] in_5,
  input  in_6,
  input  [1:0] in_7,
  input  [1:0] in_8,
  output out_9
);

  wire decoder_1_out0, decoder_1_out1, decoder_1_out2, decoder_1_out3, demultiplexer_1_out0,
       demultiplexer_1_out1, demultiplexer_1_out2, demultiplexer_1_out3;

  Demultiplexer #(.select(2)) demultiplexer_1 (
    .out0(demultiplexer_1_out0), .out1(demultiplexer_1_out1), .out2(demultiplexer_1_out2),
    .out3(demultiplexer_1_out3), .in(in_6), .sel(in_8));
  Multiplexer #(.select(2)) multiplexer_1 (.in0(A), .in1(B), .in2(C), .in3(D), .out(out_9), .sel(in_5));
  LED led_1 (.in(demultiplexer_1_out0));
  LED led_2 (.in(demultiplexer_1_out1));
  LED led_3 (.in(demultiplexer_1_out2));
  LED led_4 (.in(demultiplexer_1_out3));
  BitSelector #(.group(2)) bitselector_1 ();  // open: in, out, sel
  Decoder #(.enable("false"), .select(2)) decoder_1 (
    .out0(decoder_1_out0), .out1(decoder_1_out1), .out2(decoder_1_out2), .out3(decoder_1_out3), .sel(in_7));
  Priority_Encoder #(.select(2)) priority_encoder_1 ();  // open: in0, in1, in2, in3, out, gs, en_out, en_in
  LED led_5 (.in(decoder_1_out0));
  LED led_6 (.in(decoder_1_out1));
  LED led_7 (.in(decoder_1_out2));
  LED led_8 (.in(decoder_1_out3));
endmodule

module custom_decd (
  input  [1:0] SEL,
  output out_2,
  output out_3,
  output out_4,
  output out_5
);

  and and_1 (out_2, ~SEL[0], ~SEL[1]);  // AND_Gate
  and and_2 (out_3, SEL[0], ~SEL[1]);  // AND_Gate
  and and_3 (out_4, ~SEL[0], SEL[1]);  // AND_Gate
  and and_4 (out_5, SEL[0], SEL[1]);
endmodule

module custom_mux (
  input  A,
  input  B,
  input  C,
  input  D,
  input  [1:0] SEL,
  output X
);

  wire and_1_out, and_2_out, and_3_out, and_4_out;

  assign X = and_1_out ? A : 1'bz;  // Controlled_Buffer controlled_buffer_1
  and and_1 (and_1_out, ~SEL[0], ~SEL[1]);  // AND_Gate
  assign X = and_2_out ? B : 1'bz;  // Controlled_Buffer controlled_buffer_2
  assign X = and_3_out ? C : 1'bz;  // Controlled_Buffer controlled_buffer_3
  assign X = and_4_out ? D : 1'bz;  // Controlled_Buffer controlled_buffer_4
  and and_2 (and_2_out, SEL[0], ~SEL[1]);  // AND_Gate
  and and_3 (and_3_out, ~SEL[0], SEL[1]);  // AND_Gate
  and and_4 (and_4_out, SEL[0], SEL[1]);
endmodule
