// Logisim project hradla_gallery.circ as structural Verilog: 1 circuit, main circuit main
module main (
);

  // Buffer buffer_1 is placed but not wired
  // AND_Gate and_1 is placed but not wired
  // NOT_Gate not_1 is placed but not wired
  // NAND_Gate nand_1 is placed but not wired
  // OR_Gate or_1 is placed but not wired
  // NOR_Gate nor_1 is placed but not wired
  // XOR_Gate xor_1 is placed but not wired
  // XNOR_Gate xnor_1 is placed but not wired

  // Notes on the sheet:
  //   Buffer
  //   AND
  //   NAND
  //   NOT
  //   OR
  //   NOR
  //   XOR
  //   XNOR
endmodule
