// Logisim project karnaughova_mapa.circ as structural Verilog: 2 circuits, main circuit main
module main (
  input  A,
  input  B,
  input  C
);

  wire not_1_out, not_2_out, not_3_out, Q1_out, Q2_out;

  not not_1 (not_1_out, A);
  not not_2 (not_2_out, B);
  not not_3 (not_3_out, C);
  and Q2 (Q2_out, not_1_out, not_3_out);
  and Q1 (Q1_out, not_2_out, not_3_out);
  // OR_Gate Q has open pins: in0=Q2_out, in1=Q1_out, out=open
endmodule

module karnaughova_mapa_1 (
  input  A,
  input  B,
  input  C,
  output Q
);

  wire not_1_out, not_2_out, not_3_out, Q1_out, Q2_out;

  not not_1 (not_1_out, A);
  not not_2 (not_2_out, B);
  not not_3 (not_3_out, C);
  and Q2 (Q2_out, not_1_out, not_3_out);
  and Q1 (Q1_out, not_2_out, not_3_out);
  or or_1 (Q, Q2_out, Q1_out);
endmodule
