// Logisim project karnaughova_mapa_1.circ as structural Verilog: 1 circuit, main circuit main
module main (
  input  A,
  input  B,
  input  C,
  input  D,
  output out_5
);

  wire and_1_out, and_2_out, and_3_out, or_1_out;

  and and_1 (and_1_out, A, ~C);  // AND_Gate
  and and_2 (and_2_out, ~A, ~C, D);  // AND_Gate
  or or_1 (or_1_out, A, C, and_2_out);
  and and_3 (and_3_out, B, or_1_out);
  or or_2 (out_5, and_1_out, and_3_out);
endmodule
