// Logisim project logisim_stavy.circ as structural Verilog: 1 circuit, main circuit main
module main (
  input  in_1,
  input  in_2,
  input  in_3,
  input  in_4,
  input  in_5,
  input  in_6,
  input  in_7,
  input  in_8,
  input  in_9,
  input  in_10,
  output out_11,
  output out_12,
  output undefined,
  output zkrat,
  output out_15
);

  wire and_1_out, controlled_buffer_2_out, or_1_out;

  and and_1 (and_1_out, in_2, in_5);
  Controlled_Buffer controlled_buffer_1 (.in(and_1_out));  // open: out, en
  or or_1 (or_1_out, in_5, in_7);
  Controlled_Buffer controlled_buffer_2 (.in(or_1_out), .out(controlled_buffer_2_out));  // open: en

  assign in_8 = in_6;
  assign in_10 = in_9;
  assign out_11 = in_1;
  assign out_12 = in_3;
  assign out_15 = in_9;
  assign undefined = in_4;
  assign zkrat = in_6;
endmodule
