// Logisim project logisim_uvod.circ as structural Verilog: 2 circuits, main circuit main
module main (
  input  in_1,
  input  in_2,
  output out_3
);

  custom_and custom_and_1 (.A(in_1), .B(in_2), .C(out_3));
endmodule

module custom_and (
  input  A,
  input  B,
  output C
);

  and and_1 (C, A, B);
endmodule
