// Logisim project sekvencni_obvody.circ as structural Verilog
module kombinacni (
  input  A,
  input  B,
  input  C,
  output X,
  output Y
);

  wire or_1_out;

  or or_1 (or_1_out, A, B);
  and and_1 (Y, B, C);
  nand nand_1 (X, or_1_out, Y);
endmodule

module sekvencni (
  input  A,
  output X
);

  Pull_Resistor pull_resistor_1 (.node(X));
  or or_1 (X, X, A);
endmodule
