// Logisim project teorie_cviko_1.circ as structural Verilog: 1 circuit, main circuit main
module main (
  input  A,
  input  B,
  input  C
);

  wire and_1_out, not_1_out, xor_1_out;

  not not_1 (not_1_out, C);
  and and_1 (and_1_out, A, B);
  xor xor_1 (xor_1_out, and_1_out, not_1_out);
  // Probe on nothing

  // Notes on the sheet:
  //   X
endmodule
