// Logisim project teorie_cviko_2.circ as structural Verilog: 1 circuit, main circuit main
module main (
  input  A,
  input  B,
  input  C,
  input  D
);

  wire and_1_out, and_2_out, not_1_out, or_1_out, xnor_1_out;

  not not_1 (not_1_out, A);
  or or_1 (or_1_out, B, C);
  and and_1 (and_1_out, not_1_out, or_1_out);
  xnor xnor_1 (xnor_1_out, or_1_out, D);
  and and_2 (and_2_out, or_1_out, xnor_1_out);
  // Probe on nothing
  // Probe on nothing

  // Notes on the sheet:
  //   X
  //   Y
endmodule
