// Logisim project teorie_cviko_3.circ as structural Verilog
module main (
  input  A,
  input  B,
  input  C,
  output X
);

  wire and_1_out, not_1_out, or_1_out, xnor_1_out;

  and and_1 (and_1_out, A, B);
  not not_1 (not_1_out, B);
  xnor xnor_1 (xnor_1_out, A, C);
  or or_1 (or_1_out, and_1_out, not_1_out);
  or or_2 (X, or_1_out, xnor_1_out);
endmodule
